# Fritzing sketch EggIncubator (saved by Fritzing 0.9.3b)
circuit board: 10.6793cm x 6.70057cm
breadboards: 2

parts:
  Q1 = MOSFET-NCHANNEL [package=to220v]
  J-FAN-T = male pin header, 4 pins [form="♂ (male)"]
  J-FAN-H = male pin header, 4 pins [form="♂ (male)"]
  J-L1 = male pin header, 2 pins [form="♂ (male)"]
  J-ULN-R = female pin header, 7 pins [form="♀ (female)"]
  J-ULN-L = female pin header, 7 pins [form="♀ (female)"]
  J-L2 = male pin header, 2 pins [form="♂ (male)"]
  Q2 = MOSFET-NCHANNEL [package=to220v]
  J-L3 = male pin header, 2 pins [form="♂ (male)"]
  Q3 = MOSFET-NCHANNEL [package=to220v]
  P12V = Screw terminal - 2 pins [package=THT]
  R6 = Resistor [tolerance=±5% resistance=100 package="0805 [SMD]"]
  R5 = Resistor [tolerance=±5% resistance=100k package="0805 [SMD]"]
  R3 = Resistor [tolerance=±5% resistance=100k package="0805 [SMD]"]
  R4 = Resistor [tolerance=±5% resistance=100 package="0805 [SMD]"]
  R1 = Resistor [tolerance=±5% resistance=100k package="0805 [SMD]"]
  R2 = Resistor [tolerance=±5% resistance=100 package="0805 [SMD]"]
  J-PM = female pin header, 4 pins [form="♀ (female)"]
  Arduino = female pin header, 12 pins [form="♀ (female)"]
  Pro_mini = female pin header, 12 pins [form="♀ (female)"]
  R-DSL = Resistor [tolerance=±5% resistance=4.7k package="0805 [SMD]"]
  J-DHT11 = male pin header, 3 pins [form="♂ (male)"]
  J-SERVO = male pin header, 3 pins [form="♂ (male)"]
  R-T2 = Temperature Sensor (Thermistor) [thermistor_type=NTC package=THT]
  R6_2 = Resistor [tolerance=±5% resistance=100k package="0805 [SMD]"]
  R5_2 = Resistor [tolerance=±5% resistance=100k package="0805 [SMD]"]
  R12 = Photocell (LDR) [package=THT]
  R7 = Resistor [tolerance=±5% resistance=100k package="0805 [SMD]"]
  R-T1 = Temperature Sensor (Thermistor) [thermistor_type=NTC package=THT]
  J-M1 = male pin header, 5 pins [form="♂ (male)"]
  J-OLED = female pin header, 4 pins [form="♀ (female)"]
  R-DHT = Resistor [tolerance=±5% resistance=4.7k package="0805 [SMD]"]
  J-DS1 = male pin header, 3 pins [form="♂ (male)"]
  C1 = Electrolytic Capacitor [capacitance=4.7µF voltage=35V package="100 mil [THT, electrolytic]"]
  J-A4 = male pin header, 2 pins [form="♂ (male)"]
  J-I2C = female pin header, 5 pins [form="♀ (female)"]
  J-I2C1 = female pin header, 5 pins [form="♀ (female)"]
  J3 = male pin header, 3 pins [form="♂ (male)"]
  R8 = Resistor [tolerance=±5% resistance=4.7k package="0805 [SMD]"]
  J4 = male pin header, 3 pins [form="♂ (male)"]
  R11 = Resistor [tolerance=±5% resistance=10k package=THT]
  R10 = Resistor [tolerance=±5% resistance=100k package=THT]
  C2 = Electrolytic Capacitor [capacitance=4.7µF voltage=35V package="100 mil [THT, electrolytic]"]
  R9 = Resistor [tolerance=±5% resistance=4.7k power=1W package=THT]

nets (from the pcb view):
  N1: Q1.G, R1.Pin_0, R2.Pin_1
  N2: Q1.D, J-L1.pin1
  N3: Q1.S, Q2.S, Q3.S, P12V.pin1, R5.Pin_1, R3.Pin_1, R1.Pin_1, J-PM.pin1, Arduino.pin4, Pro_mini.pin2, J-DHT11.pin3, J-SERVO.pin3, R-T2.pin_0, R12.pin_0, R-T1.pin_0, J-OLED.pin4, J-DS1.pin3, C1.-, J-I2C.pin5, J-I2C1.pin5, J3.pin3, J4.pin3, R11.Pin_1, C2.-
  N4: J-FAN-T.pin1, J-ULN-L.pin6, J-ULN-L.pin7, Arduino.pin11
  N5: J-FAN-T.pin3, J-FAN-H.pin3, J-L1.pin2, J-L2.pin2, J-L3.pin2, P12V.pin2, J-PM.pin2, Pro_mini.pin1, J-M1.pin5, C1.+, R10.Pin_0, C2.+
  N6: J-FAN-T.pin4, J4.pin2
  N7: J-FAN-H.pin1, J-ULN-L.pin5, Arduino.pin10
  N8: J-FAN-H.pin4, J3.pin2
  N9: J-ULN-R.pin1, J-M1.pin1
  N10: J-ULN-R.pin2, J-M1.pin2
  N11: J-ULN-R.pin3, J-M1.pin3
  N12: J-ULN-R.pin4, J-M1.pin4
  N13: J-ULN-R.pin5, J4.pin1
  N14: J-ULN-R.pin6, J-ULN-R.pin7, J3.pin1
  N15: J-ULN-L.pin1, Pro_mini.pin9
  N16: J-ULN-L.pin2, Pro_mini.pin10
  N17: J-ULN-L.pin3, Pro_mini.pin11
  N18: J-ULN-L.pin4, Pro_mini.pin12
  N19: J-L2.pin1, Q2.D
  N20: Q2.G, R3.Pin_0, R4.Pin_1
  N21: J-L3.pin1, Q3.D
  N22: Q3.G, R6.Pin_1, R5.Pin_0
  N23: R6.Pin_0, Arduino.pin12
  N24: R4.Pin_0, Arduino.pin9
  N25: R2.Pin_0, Arduino.pin8
  N26: J-PM.pin3, J-PM.pin4
  N27: Arduino.pin5, R-DSL.Pin_1, J-DS1.pin1
  N28: Arduino.pin6, J-SERVO.pin1
  N29: Arduino.pin7, J-DHT11.pin1, R-DHT.Pin_1
  N30: Pro_mini.pin4, R-DSL.Pin_0, J-DHT11.pin2, J-SERVO.pin2, R6_2.Pin_0, R5_2.Pin_0, R7.Pin_0, J-OLED.pin3, R-DHT.Pin_0, J-DS1.pin2, J-I2C.pin4, J-I2C1.pin4, R8.Pin_0, R9.Pin_0
  N31: Pro_mini.pin5, R11.Pin_0, R10.Pin_1
  N32: Pro_mini.pin6, R5_2.Pin_1, R12.pin_1
  N33: Pro_mini.pin7, R-T2.pin_1, R6_2.Pin_1
  N34: Pro_mini.pin8, R7.Pin_1, R-T1.pin_1
  N35: J-OLED.pin1, J-A4.pin1, J-I2C.pin2, J-I2C1.pin2, R9.Pin_1
  N36: J-OLED.pin2, J-A4.pin2, J-I2C.pin3, J-I2C1.pin3, R8.Pin_1
  N37: J-I2C.pin1, J-I2C1.pin1
